// Logisim project connectfour.circ as structural Verilog: 6 circuits, main circuit main
module main (
);

  wire button_1_out, button_2_out, button_3_out, button_4_out, button_5_out, button_6_out, button_7_out,
       game_1_win;

  Button button_1 (.out(button_1_out));
  Button button_2 (.out(button_2_out));
  game game_1 (
    .Win(game_1_win), .Play1(button_1_out), .Play2(button_2_out), .Play3(button_3_out), .Play4(button_4_out),
    .Play5(button_5_out), .Play6(button_6_out), .Play7(button_7_out));  // open: Current_player, out_93, out_8, out_15, out_22, out_29, out_36, Column_storage, out_50, out_57, out_64, out_71, out_78, out_85, out_9, out_16, out_23, out_30, out_37, out_44, out_51, out_58, out_65, out_72, out_79, out_86, out_10, out_17, out_24, out_31, out_38, out_45, out_52, out_59, out_66, out_73, out_80, out_87, out_11, out_18, out_25, out_32, out_39, out_46, out_53, out_60, out_67, out_74, out_81, out_88, out_12, out_19, out_26, out_33, out_40, out_47, out_54, out_61, out_68, out_75, out_82, out_89, out_13, out_20, out_27, out_34, out_41, out_48, out_55, out_62, out_69, out_76, out_83, out_90, out_14, out_21, out_28, out_35, out_42, out_49, out_56, out_63, out_70, out_77, out_84, out_91
  // RGBLED rgbled_1: pin names not known
  // RGBLED rgbled_2: pin names not known
  // RGBLED rgbled_3: pin names not known
  // RGBLED rgbled_4: pin names not known
  // RGBLED rgbled_5: pin names not known
  // RGBLED rgbled_6: pin names not known
  // RGBLED rgbled_7: pin names not known
  // RGBLED rgbled_8: pin names not known
  // RGBLED rgbled_9: pin names not known
  // RGBLED rgbled_10: pin names not known
  // RGBLED rgbled_11: pin names not known
  // RGBLED rgbled_12: pin names not known
  // RGBLED rgbled_13: pin names not known
  // RGBLED rgbled_14: pin names not known
  // RGBLED rgbled_15: pin names not known
  // RGBLED rgbled_16: pin names not known
  // RGBLED rgbled_17: pin names not known
  // RGBLED rgbled_18: pin names not known
  Button button_3 (.out(button_3_out));
  Button button_4 (.out(button_4_out));
  Button button_5 (.out(button_5_out));
  // RGBLED rgbled_19: pin names not known
  // RGBLED rgbled_20: pin names not known
  // RGBLED rgbled_21: pin names not known
  // RGBLED rgbled_22: pin names not known
  // RGBLED rgbled_23: pin names not known
  // RGBLED rgbled_24: pin names not known
  // RGBLED rgbled_25: pin names not known
  // RGBLED rgbled_26: pin names not known
  // RGBLED rgbled_27: pin names not known
  // RGBLED rgbled_28: pin names not known
  // RGBLED rgbled_29: pin names not known
  // RGBLED rgbled_30: pin names not known
  Button button_6 (.out(button_6_out));
  Button button_7 (.out(button_7_out));
  // RGBLED rgbled_31: pin names not known
  // RGBLED rgbled_32: pin names not known
  // RGBLED rgbled_33: pin names not known
  // RGBLED rgbled_34: pin names not known
  // RGBLED rgbled_35: pin names not known
  // RGBLED rgbled_36: pin names not known
  // RGBLED rgbled_37: pin names not known
  // RGBLED rgbled_38: pin names not known
  // RGBLED rgbled_39: pin names not known
  // RGBLED rgbled_40: pin names not known
  // RGBLED rgbled_41: pin names not known
  // RGBLED rgbled_42: pin names not known
  // RGBLED rgbled_43: pin names not known
  LED led_1 (.in(game_1_win));
endmodule

module game (
  input  Play1,
  input  Play2,
  input  Play3,
  input  Play4,
  input  Play5,
  input  Play6,
  input  Play7,
  output out_8,
  output out_9,
  output out_10,
  output out_11,
  output out_12,
  output out_13,
  output out_14,
  output out_15,
  output out_16,
  output out_17,
  output out_18,
  output out_19,
  output out_20,
  output out_21,
  output out_22,
  output out_23,
  output out_24,
  output out_25,
  output out_26,
  output out_27,
  output out_28,
  output out_29,
  output out_30,
  output out_31,
  output out_32,
  output out_33,
  output out_34,
  output out_35,
  output out_36,
  output out_37,
  output out_38,
  output out_39,
  output out_40,
  output out_41,
  output out_42,
  output Column_storage,
  output out_44,
  output out_45,
  output out_46,
  output out_47,
  output out_48,
  output out_49,
  output out_50,
  output out_51,
  output out_52,
  output out_53,
  output out_54,
  output out_55,
  output out_56,
  output out_57,
  output out_58,
  output out_59,
  output out_60,
  output out_61,
  output out_62,
  output out_63,
  output out_64,
  output out_65,
  output out_66,
  output out_67,
  output out_68,
  output out_69,
  output out_70,
  output out_71,
  output out_72,
  output out_73,
  output out_74,
  output out_75,
  output out_76,
  output out_77,
  output out_78,
  output out_79,
  output out_80,
  output out_81,
  output out_82,
  output out_83,
  output out_84,
  output out_85,
  output out_86,
  output out_87,
  output out_88,
  output out_89,
  output out_90,
  output out_91,
  output Current_player,
  output out_93,
  output Win
);

  wire and_1_out, and_2_out, column_store_1_out_15, column_store_2_out_15, column_store_3_out_15,
       column_store_4_out_15, column_store_5_out_15, column_store_6_out_15, column_store_7_out_15, or_1_out,
       or_2_out, or_3_out, or_4_out, or_5_out, or_6_out, or_7_out, or_8_out, or_9_out, or_10_out, or_11_out,
       win_column_1_win, win_column_2_win, win_column_3_win, win_column_4_win, win_column_5_win,
       win_column_6_win, win_column_7_win, win_column_8_win, win_column_9_win, win_column_10_win,
       win_column_11_win, win_column_12_win, win_column_13_win, win_column_14_win, win_grid_1_win,
       win_grid_2_win;
  wire [5:0] column_store_1_out_4, column_store_1_out_18, column_store_2_out_4, column_store_2_out_18,
       column_store_3_out_4, column_store_3_out_18, column_store_4_out_4, column_store_4_out_18,
       column_store_5_out_4, column_store_5_out_18, column_store_6_out_4, column_store_6_out_18,
       column_store_7_out_4, column_store_7_out_18;

  and and_1 (and_1_out, ~or_2_out, or_3_out);  // AND_Gate
  or or_1 (or_1_out, Play1, Play2, Play3, Play4, Play5, Play6, Play7);
  and and_2 (and_2_out, or_1_out, Win);
  T_Flip_Flop #(.trigger("falling")) t_ff_1 (
    .clk(or_1_out), .T(and_1_out), .Q(Current_player), .Qn(out_93));  // open: preset, reset
  or or_2 (or_2_out, win_grid_1_win, win_grid_2_win, or_4_out);
  D_Flip_Flop #(.trigger("falling")) d_ff_1 (
    .D(or_2_out), .clk(or_1_out), .Q(Win), .reset(and_2_out));  // open: Qn, preset
  column_store column_store_1 (
    .out_15(column_store_1_out_15), .out_4(column_store_1_out_4), .out_18(column_store_1_out_18),
    .out_5(out_8), .out_6(out_15), .out_7(out_22), .out_8(out_29), .out_9(out_36), .out_10(Column_storage),
    .out_11(out_50), .out_12(out_57), .out_13(out_64), .out_14(out_71), .out_16(out_78), .out_17(out_85),
    .Reset(and_2_out), .Play(Play1), .Turn(Current_player));
  or or_3 (or_3_out, column_store_1_out_15, column_store_2_out_15, column_store_3_out_15, column_store_4_out_15, column_store_5_out_15, column_store_6_out_15, column_store_7_out_15);
  win_grid win_grid_1 (
    .Win(win_grid_1_win), .Column1(column_store_1_out_18), .Column2(column_store_2_out_18),
    .Column3(column_store_3_out_18), .Column4(column_store_4_out_18), .Column5(column_store_5_out_18),
    .Column6(column_store_6_out_18), .Column7(column_store_7_out_18));
  win_grid win_grid_2 (
    .Win(win_grid_2_win), .Column1(column_store_1_out_4), .Column2(column_store_2_out_4),
    .Column3(column_store_3_out_4), .Column4(column_store_4_out_4), .Column5(column_store_5_out_4),
    .Column6(column_store_6_out_4), .Column7(column_store_7_out_4));
  or or_4 (or_4_out, or_5_out, or_6_out, or_7_out, or_8_out, or_9_out, or_10_out, or_11_out);
  win_column win_column_1 (.Win(win_column_1_win), .Column(column_store_1_out_18));
  win_column win_column_2 (.Win(win_column_2_win), .Column(column_store_1_out_4));
  or or_5 (or_5_out, win_column_1_win, win_column_2_win);
  column_store column_store_2 (
    .out_15(column_store_2_out_15), .out_4(column_store_2_out_4), .out_18(column_store_2_out_18),
    .out_5(out_9), .out_6(out_16), .out_7(out_23), .out_8(out_30), .out_9(out_37), .out_10(out_44),
    .out_11(out_51), .out_12(out_58), .out_13(out_65), .out_14(out_72), .out_16(out_79), .out_17(out_86),
    .Reset(and_2_out), .Play(Play2), .Turn(Current_player));
  win_column win_column_3 (.Win(win_column_3_win), .Column(column_store_2_out_18));
  win_column win_column_4 (.Win(win_column_4_win), .Column(column_store_2_out_4));
  or or_6 (or_6_out, win_column_3_win, win_column_4_win);
  column_store column_store_3 (
    .out_15(column_store_3_out_15), .out_4(column_store_3_out_4), .out_18(column_store_3_out_18),
    .out_5(out_10), .out_6(out_17), .out_7(out_24), .out_8(out_31), .out_9(out_38), .out_10(out_45),
    .out_11(out_52), .out_12(out_59), .out_13(out_66), .out_14(out_73), .out_16(out_80), .out_17(out_87),
    .Reset(and_2_out), .Play(Play3), .Turn(Current_player));
  win_column win_column_5 (.Win(win_column_5_win), .Column(column_store_3_out_18));
  win_column win_column_6 (.Win(win_column_6_win), .Column(column_store_3_out_4));
  or or_7 (or_7_out, win_column_5_win, win_column_6_win);
  column_store column_store_4 (
    .out_15(column_store_4_out_15), .out_4(column_store_4_out_4), .out_18(column_store_4_out_18),
    .out_5(out_11), .out_6(out_18), .out_7(out_25), .out_8(out_32), .out_9(out_39), .out_10(out_46),
    .out_11(out_53), .out_12(out_60), .out_13(out_67), .out_14(out_74), .out_16(out_81), .out_17(out_88),
    .Reset(and_2_out), .Play(Play4), .Turn(Current_player));
  win_column win_column_7 (.Win(win_column_7_win), .Column(column_store_4_out_18));
  win_column win_column_8 (.Win(win_column_8_win), .Column(column_store_4_out_4));
  or or_8 (or_8_out, win_column_7_win, win_column_8_win);
  column_store column_store_5 (
    .out_15(column_store_5_out_15), .out_4(column_store_5_out_4), .out_18(column_store_5_out_18),
    .out_5(out_12), .out_6(out_19), .out_7(out_26), .out_8(out_33), .out_9(out_40), .out_10(out_47),
    .out_11(out_54), .out_12(out_61), .out_13(out_68), .out_14(out_75), .out_16(out_82), .out_17(out_89),
    .Reset(and_2_out), .Play(Play5), .Turn(Current_player));
  win_column win_column_9 (.Win(win_column_9_win), .Column(column_store_5_out_18));
  or or_9 (or_9_out, win_column_9_win, win_column_10_win);
  column_store column_store_6 (
    .out_15(column_store_6_out_15), .out_4(column_store_6_out_4), .out_18(column_store_6_out_18),
    .out_5(out_13), .out_6(out_20), .out_7(out_27), .out_8(out_34), .out_9(out_41), .out_10(out_48),
    .out_11(out_55), .out_12(out_62), .out_13(out_69), .out_14(out_76), .out_16(out_83), .out_17(out_90),
    .Reset(and_2_out), .Play(Play6), .Turn(Current_player));
  win_column win_column_10 (.Win(win_column_10_win), .Column(column_store_5_out_4));
  win_column win_column_11 (.Win(win_column_11_win), .Column(column_store_6_out_18));
  column_store column_store_7 (
    .out_15(column_store_7_out_15), .out_4(column_store_7_out_4), .out_18(column_store_7_out_18),
    .out_5(out_14), .out_6(out_21), .out_7(out_28), .out_8(out_35), .out_9(out_42), .out_10(out_49),
    .out_11(out_56), .out_12(out_63), .out_13(out_70), .out_14(out_77), .out_16(out_84), .out_17(out_91),
    .Reset(and_2_out), .Play(Play7), .Turn(Current_player));
  win_column win_column_12 (.Win(win_column_12_win), .Column(column_store_6_out_4));
  or or_10 (or_10_out, win_column_11_win, win_column_12_win);
  win_column win_column_13 (.Win(win_column_13_win), .Column(column_store_7_out_18));
  win_column win_column_14 (.Win(win_column_14_win), .Column(column_store_7_out_4));
  or or_11 (or_11_out, win_column_13_win, win_column_14_win);

  // Notes on the sheet:
  //   Check row & diagonal win
  //   Win state
  //   Check column win
  //   Column inputs
endmodule

module column_store (
  input  Play,
  input  Turn,
  input  Reset,
  output [5:0] out_4,
  output out_5,
  output out_6,
  output out_7,
  output out_8,
  output out_9,
  output out_10,
  output out_11,
  output out_12,
  output out_13,
  output out_14,
  output out_15,
  output out_16,
  output out_17,
  output [5:0] out_18
);

  wire d_ff_1_qn, decoder_1_out0, decoder_1_out1;
  wire [2:0] priority_encoder_1_out;
  wire [5:0] multiplexer_1_out, or_1_out, or_2_out;
  wire [7:0] shifter_1_out;

  and and_1 (out_15, Play, d_ff_1_qn);
  Decoder decoder_1 (.out0(decoder_1_out0), .out1(decoder_1_out1), .sel(Turn));  // open: en
  Register #(.width(6)) register_1 (.D(or_2_out), .en(decoder_1_out0), .Q(out_4), .clk(out_15), .clr(Reset));
  Register #(.width(6)) register_2 (
    .D(or_2_out), .en(decoder_1_out1), .Q({out_11, out_12, out_13, out_14, out_16, out_17}), .clk(out_15),
    .clr(Reset));
  assign or_1_out = out_4 | {out_11, out_12, out_13, out_14, out_16, out_17};  // OR_Gate or_1, 6 bits wide
  Priority_Encoder priority_encoder_1 (
    .in0(1'b1), .in1(or_1_out[0]), .in2(or_1_out[1]), .in3(or_1_out[2]), .in4(or_1_out[3]),
    .in5(or_1_out[4]), .in6(or_1_out[5]), .out(priority_encoder_1_out));  // open: in7, en_in, gs, en_out
  D_Flip_Flop #(.trigger("falling")) d_ff_1 (
    .clk(Play), .D(or_1_out[5]), .Qn(d_ff_1_qn), .reset(Reset));  // open: Q, preset
  Shifter shifter_1 (.in(8'h1), .\dist (priority_encoder_1_out), .out(shifter_1_out));
  Multiplexer #(.enable("false"), .width(6)) multiplexer_1 (
    .in0(out_4), .in1({out_11, out_12, out_13, out_14, out_16, out_17}), .out(multiplexer_1_out), .sel(Turn));
  assign or_2_out = multiplexer_1_out | shifter_1_out[5:0];  // OR_Gate or_2, 6 bits wide

  assign out_5 = out_4[5];
  assign out_6 = out_4[4];
  assign out_7 = out_4[3];
  assign out_8 = out_4[2];
  assign out_9 = out_4[1];
  assign out_10 = out_4[0];
  assign out_18 = {out_11, out_12, out_13, out_14, out_16, out_17};
endmodule

module win_column (
  input  [5:0] Column,
  output Win
);

  wire comparator_1_eq, comparator_2_eq, comparator_3_eq;

  Comparator #(.mode("unsigned"), .width(4)) comparator_1 (
    .a(Column[3:0]), .b(4'b1111), .eq(comparator_1_eq));  // open: gt, lt
  Comparator #(.mode("unsigned"), .width(4)) comparator_2 (
    .a(Column[4:1]), .b(4'b1111), .eq(comparator_2_eq));  // open: gt, lt
  Comparator #(.mode("unsigned"), .width(4)) comparator_3 (
    .a(Column[5:2]), .b(4'b1111), .eq(comparator_3_eq));  // open: gt, lt
  or or_1 (Win, comparator_1_eq, comparator_2_eq, comparator_3_eq);
endmodule

module win_row (
  input  [6:0] Row,
  output Win
);

  wire comparator_1_eq, comparator_2_eq, comparator_3_eq, comparator_4_eq;

  Comparator #(.mode("unsigned"), .width(4)) comparator_1 (
    .a(Row[3:0]), .b(4'b1111), .eq(comparator_1_eq));  // open: gt, lt
  Comparator #(.mode("unsigned"), .width(4)) comparator_2 (
    .a(Row[4:1]), .b(4'b1111), .eq(comparator_2_eq));  // open: gt, lt
  Comparator #(.mode("unsigned"), .width(4)) comparator_3 (
    .a(Row[5:2]), .b(4'b1111), .eq(comparator_3_eq));  // open: gt, lt
  Comparator #(.mode("unsigned"), .width(4)) comparator_4 (
    .a(Row[6:3]), .b(4'b1111), .eq(comparator_4_eq));  // open: gt, lt
  or or_1 (Win, comparator_1_eq, comparator_2_eq, comparator_3_eq, comparator_4_eq);
endmodule

module win_grid (
  input  [5:0] Column1,
  input  [5:0] Column2,
  input  [5:0] Column3,
  input  [5:0] Column4,
  input  [5:0] Column5,
  input  [5:0] Column6,
  input  [5:0] Column7,
  output Win
);

  wire or_2_out, or_3_out, or_4_out, win_row_1_win, win_row_2_win, win_row_3_win, win_row_4_win,
       win_row_5_win, win_row_6_win, win_row_7_win, win_row_8_win, win_row_9_win, win_row_10_win,
       win_row_11_win, win_row_12_win, win_row_13_win, win_row_14_win, win_row_15_win, win_row_16_win,
       win_row_17_win, win_row_18_win;
  wire [0:0] undriven_4, undriven_10;
  wire [1:0] undriven_5, undriven_11;
  wire [2:0] undriven_6, undriven_12;
  wire [6:4] undriven, undriven_7;
  wire [6:5] undriven_2, undriven_8;
  wire [6:6] undriven_3, undriven_9;

  or or_1 (Win, or_4_out, or_3_out, or_2_out);
  or or_2 (or_2_out, win_row_1_win, win_row_2_win, win_row_3_win, win_row_4_win, win_row_5_win, win_row_6_win);
  or or_3 (or_3_out, win_row_7_win, win_row_8_win, win_row_9_win, win_row_10_win, win_row_11_win, win_row_12_win);
  or or_4 (or_4_out, win_row_13_win, win_row_14_win, win_row_15_win, win_row_16_win, win_row_17_win, win_row_18_win);
  win_row win_row_1 (
    .Win(win_row_1_win),
    .Row({Column7[0], Column6[0], Column5[0], Column4[0], Column3[0], Column2[0], Column1[0]}));
  win_row win_row_2 (
    .Win(win_row_2_win),
    .Row({Column7[1], Column6[1], Column5[1], Column4[1], Column3[1], Column2[1], Column1[1]}));
  win_row win_row_3 (
    .Win(win_row_3_win),
    .Row({Column7[2], Column6[2], Column5[2], Column4[2], Column3[2], Column2[2], Column1[2]}));
  win_row win_row_4 (
    .Win(win_row_4_win),
    .Row({Column7[3], Column6[3], Column5[3], Column4[3], Column3[3], Column2[3], Column1[3]}));
  win_row win_row_5 (
    .Win(win_row_5_win),
    .Row({Column7[4], Column6[4], Column5[4], Column4[4], Column3[4], Column2[4], Column1[4]}));
  win_row win_row_6 (
    .Win(win_row_6_win),
    .Row({Column7[5], Column6[5], Column5[5], Column4[5], Column3[5], Column2[5], Column1[5]}));
  win_row win_row_7 (.Win(win_row_7_win), .Row({undriven, Column4[0], Column3[1], Column2[2], Column1[3]}));
  win_row win_row_8 (
    .Win(win_row_8_win), .Row({undriven_2, Column5[0], Column4[1], Column3[2], Column2[3], Column1[4]}));
  win_row win_row_9 (
    .Win(win_row_9_win),
    .Row({undriven_3[6], Column6[0], Column5[1], Column4[2], Column3[3], Column2[4], Column1[5]}));
  win_row win_row_10 (
    .Win(win_row_10_win),
    .Row({Column7[0], Column6[1], Column5[2], Column4[3], Column3[4], Column2[5], undriven_4[0]}));
  win_row win_row_11 (
    .Win(win_row_11_win), .Row({Column7[1], Column6[2], Column5[3], Column4[4], Column3[5], undriven_5}));
  win_row win_row_12 (.Win(win_row_12_win), .Row({Column7[2], Column6[3], Column5[4], Column4[5], undriven_6}));
  win_row win_row_13 (.Win(win_row_13_win), .Row({undriven_7, Column4[5], Column3[4], Column2[3], Column1[2]}));
  win_row win_row_14 (
    .Win(win_row_14_win), .Row({undriven_8, Column5[5], Column4[4], Column3[3], Column2[2], Column1[1]}));
  win_row win_row_15 (
    .Win(win_row_15_win),
    .Row({undriven_9[6], Column6[5], Column5[4], Column4[3], Column3[2], Column2[1], Column1[0]}));
  win_row win_row_16 (
    .Win(win_row_16_win),
    .Row({Column7[5], Column6[4], Column5[3], Column4[2], Column3[1], Column2[0], undriven_10[0]}));
  win_row win_row_17 (
    .Win(win_row_17_win), .Row({Column7[4], Column6[3], Column5[2], Column4[1], Column3[0], undriven_11}));
  win_row win_row_18 (.Win(win_row_18_win), .Row({Column7[3], Column6[2], Column5[1], Column4[0], undriven_12}));

  // Notes on the sheet:
  //   Check row
  //   Check diagonal
  //   Check antidiagonal
endmodule
